// Digital circuit lab09.dig as structural Verilog
module lab09 (
  input  P5,
  input  reset,
  input  clock,
  input  P10,
  input  P20,
  input  Pcoffee,
  input  Ptea,
  input  Pchange,
  input  Pnext,
  output [3:0] state,
  output [5:0] Balance,
  output CoffeeOut,
  output TeaOut,
  output [1:0] Change5,
  output [1:0] Change10,
  output [1:0] Change20
);

  wire and_1_out, and_2_out, and_3_out, and_4_out, and_5_out, and_6_out, and_7_out, and_8_out, and_9_out,
       and_10_out, and_11_out, and_12_out, comparator_1_lt, comparator_2_lt, comparator_3_lt,
       comparator_4_gt, comparator_5_gt, comparator_6_gt, comparator_7_lt, comparator_8_lt, d_ff_1_nq,
       d_ff_2_nq, d_ff_3_nq, d_ff_4_nq, d_ff_5_nq, d_ff_6_nq, d_ff_7_nq, multiplexer_1_out,
       multiplexer_7_out, not_1_out, not_2_out, not_3_out, not_4_out, not_5_out, not_6_out, not_7_out,
       not_8_out, P5_t, P10_t, P20_t, Pchange_t, Pcoffee_t, Pnext_t, Ptea_t;
  wire [1:0] add_1_s, add_2_s, add_6_s, lookuptable_1_out, lookuptable_2_out, multiplexer_2_out,
       multiplexer_3_out, multiplexer_5_out;
  wire [3:0] AddCoinState, CoinChangeState, Idle7, multiplexer_6_out, multiplexer_8_out, multiplexer_9_out,
       multiplexer_10_out, multiplexer_11_out, multiplexer_12_out, multiplexer_13_out;
  wire [5:0] add_3_s, add_4_s, add_5_s, multiplexer_4_out, sub_1_s, sub_2_s, sub_3_s, sub_4_s;

  D_FF d_ff_1 (.D(P5), .C(clock), .nQ(d_ff_1_nq));  // open: Q
  D_FF d_ff_2 (.D(P10), .C(clock), .nQ(d_ff_2_nq));  // open: Q
  D_FF d_ff_3 (.D(P20), .C(clock), .nQ(d_ff_3_nq));  // open: Q
  D_FF d_ff_4 (.D(Pcoffee), .C(clock), .nQ(d_ff_4_nq));  // open: Q
  D_FF d_ff_5 (.D(Ptea), .C(clock), .nQ(d_ff_5_nq));  // open: Q
  D_FF d_ff_6 (.D(Pchange), .C(clock), .nQ(d_ff_6_nq));  // open: Q
  D_FF d_ff_7 (.D(Pnext), .C(clock), .nQ(d_ff_7_nq));  // open: Q
  LookUpTable #(.Bits(2)) lookuptable_1 (
    .in0(state[0]), .in1(state[1]), .in2(state[2]), .in3(state[3]), .out(lookuptable_1_out));
  and and_1 (and_1_out, d_ff_1_nq, P5);
  and and_2 (and_2_out, d_ff_2_nq, P10);
  and and_3 (and_3_out, d_ff_3_nq, P20);
  and and_4 (and_4_out, d_ff_4_nq, Pcoffee);
  and and_5 (and_5_out, d_ff_5_nq, Ptea);
  and and_6 (and_6_out, d_ff_6_nq, Pchange);
  and and_7 (and_7_out, d_ff_7_nq, Pnext);
  Multiplexer #(.Selector_Bits(2)) multiplexer_1 (
    .sel(lookuptable_1_out), .in_0(TeaOut), .in_1(1'b0), .in_2(1'b1), .in_3(1'b0), .out(multiplexer_1_out));
  D_FF d_ff_8 (.D(and_1_out), .C(clock), .Q(P5_t));  // open: nQ
  D_FF d_ff_9 (.D(and_2_out), .C(clock), .Q(P10_t));  // open: nQ
  D_FF d_ff_10 (.D(and_3_out), .C(clock), .Q(P20_t));  // open: nQ
  D_FF d_ff_11 (.D(and_4_out), .C(clock), .Q(Pcoffee_t));  // open: nQ
  D_FF d_ff_12 (.D(and_5_out), .C(clock), .Q(Ptea_t));  // open: nQ
  D_FF d_ff_13 (.D(and_6_out), .C(clock), .Q(Pchange_t));  // open: nQ
  D_FF d_ff_14 (.D(and_7_out), .C(clock), .Q(Pnext_t));  // open: nQ
  D_FF d_ff_15 (.D(multiplexer_1_out), .C(clock), .Q(TeaOut));  // open: nQ
  Add #(.Bits(2)) add_1 (.a(Change5), .b(2'b01), .c_i(1'b0), .s(add_1_s));  // open: c_o
  Multiplexer #(.Selector_Bits(4), .Bits(2)) multiplexer_2 (
    .sel(state), .in_0(2'b00), .in_1(Change5), .in_2(Change5), .in_3(Change5), .in_4(Change5),
    .in_5(Change5), .in_6(Change5), .in_7(Change5), .in_8(Change5), .in_9(add_1_s), .in_10(Change5),
    .in_11(Change5), .in_12(Change5), .in_13(Change5), .in_14(Change5), .in_15(2'b00), .out(multiplexer_2_out));
  D_FF #(.Bits(2)) u_Change5 (.D(multiplexer_2_out), .C(clock), .Q(Change5));  // open: nQ
  Sub #(.Bits(6)) sub_1 (.a(Balance), .b(6'b010100), .c_i(1'b0), .s(sub_1_s));  // open: c_o
  Sub #(.Bits(6)) sub_2 (.a(Balance), .b(6'b001010), .c_i(1'b0), .s(sub_2_s));  // open: c_o
  Sub #(.Bits(6)) sub_3 (.a(Balance), .b(6'b000101), .c_i(1'b0), .s(sub_3_s));  // open: c_o
  Sub #(.Bits(6)) sub_4 (.a(Balance), .b(6'b011001), .c_i(1'b0), .s(sub_4_s));  // open: c_o
  Add #(.Bits(2)) add_2 (.a(Change10), .b(2'b01), .c_i(1'b0), .s(add_2_s));  // open: c_o
  Add #(.Bits(6)) add_3 (.a(Balance), .b(6'b000101), .c_i(1'b0), .s(add_3_s));  // open: c_o
  Add #(.Bits(6)) add_4 (.a(Balance), .b(6'b001010), .c_i(1'b0), .s(add_4_s));  // open: c_o
  Add #(.Bits(6)) add_5 (.a(Balance), .b(6'b010100), .c_i(1'b0), .s(add_5_s));  // open: c_o
  Multiplexer #(.Selector_Bits(4), .Bits(2)) multiplexer_3 (
    .sel(state), .in_0(2'b00), .in_1(Change10), .in_2(Change10), .in_3(Change10), .in_4(Change10),
    .in_5(Change10), .in_6(Change10), .in_7(Change10), .in_8(add_2_s), .in_9(Change10), .in_10(Change10),
    .in_11(Change10), .in_12(Change10), .in_13(Change10), .in_14(Change10), .in_15(2'b00),
    .out(multiplexer_3_out));
  D_FF #(.Bits(2)) u_Change10 (.D(multiplexer_3_out), .C(clock), .Q(Change10));  // open: nQ
  Comparator #(.Bits(6)) comparator_1 (.a(Balance), .b(6'b000101), .lt(comparator_1_lt));  // open: gt, eq
  Comparator #(.Bits(6)) comparator_2 (.a(Balance), .b(6'b001010), .lt(comparator_2_lt));  // open: gt, eq
  Comparator #(.Bits(6)) comparator_3 (.a(Balance), .b(6'b010100), .lt(comparator_3_lt));  // open: gt, eq
  Multiplexer #(.Bits(6), .Selector_Bits(4)) multiplexer_4 (
    .sel(state), .in_0({6{1'b0}}), .in_1(Balance), .in_2(add_3_s), .in_3(add_4_s), .in_4(add_5_s),
    .in_5(sub_4_s), .in_6(sub_1_s), .in_7(Balance), .in_8(sub_2_s), .in_9(sub_3_s), .in_10(Balance),
    .in_11(Balance), .in_12(sub_1_s), .in_13(Balance), .in_14(Balance), .in_15(Balance),
    .out(multiplexer_4_out));
  not not_1 (not_1_out, comparator_1_lt);
  not not_2 (not_2_out, comparator_2_lt);
  not not_3 (not_3_out, comparator_3_lt);
  Add #(.Bits(2)) add_6 (.a(Change20), .b(2'b01), .c_i(1'b0), .s(add_6_s));  // open: c_o
  D_FF #(.Bits(6)) u_Balance (.D(multiplexer_4_out), .C(clock), .Q(Balance));  // open: nQ
  Multiplexer #(.Bits(2), .Selector_Bits(4)) multiplexer_5 (
    .sel(state), .in_0(2'b00), .in_1(Change20), .in_2(Change20), .in_3(Change20), .in_4(Change20),
    .in_5(Change20), .in_6(Change20), .in_7(Change20), .in_8(Change20), .in_9(Change20), .in_10(Change20),
    .in_11(Change20), .in_12(add_6_s), .in_13(Change20), .in_14(Change20), .in_15(2'b00),
    .out(multiplexer_5_out));
  LookUpTable #(.Bits(4)) CoinChangeTable (.in0(not_1_out), .in1(not_2_out), .in2(not_3_out), .out(CoinChangeState));
  D_FF #(.Bits(2)) u_Change20 (.D(multiplexer_5_out), .C(clock), .Q(Change20));  // open: nQ
  LookUpTable #(.Bits(2)) lookuptable_2 (
    .in0(state[0]), .in1(state[1]), .in2(state[2]), .in3(state[3]), .out(lookuptable_2_out));
  Multiplexer #(.Bits(4), .Selector_Bits(4)) multiplexer_6 (
    .sel(state), .in_0(4'b0001), .in_1(AddCoinState), .in_2(4'b0001), .in_3(4'b0001), .in_4(4'b0001),
    .in_5(4'b0111), .in_6(4'b0111), .in_7(Idle7), .in_8(4'b1101), .in_9(4'b1101), .in_10(4'b0000),
    .in_11(4'b0000), .in_12(4'b1101), .in_13(CoinChangeState), .in_14(4'b0000), .in_15(4'b1101),
    .out(multiplexer_6_out));
  Multiplexer #(.Selector_Bits(2)) multiplexer_7 (
    .sel(lookuptable_2_out), .in_0(CoffeeOut), .in_1(1'b0), .in_2(1'b1), .in_3(1'b0), .out(multiplexer_7_out));
  Comparator #(.Bits(6)) comparator_4 (.a(Balance), .b(6'b101101), .gt(comparator_4_gt));  // open: eq, lt
  D_FF #(.Bits(4)) u_State (.D(multiplexer_6_out), .C(clock), .Q(state));  // open: nQ
  Comparator #(.Bits(6)) comparator_5 (.a(Balance), .b(6'b101000), .gt(comparator_5_gt));  // open: eq, lt
  D_FF d_ff_16 (.D(multiplexer_7_out), .C(clock), .Q(CoffeeOut));  // open: nQ
  and and_8 (and_8_out, P5_t, not_4_out);
  not not_4 (not_4_out, comparator_4_gt);
  not not_5 (not_5_out, comparator_5_gt);
  Comparator #(.Bits(6)) comparator_6 (.a(Balance), .b(6'b011110), .gt(comparator_6_gt));  // open: eq, lt
  and and_9 (and_9_out, P10_t, not_5_out);
  not not_6 (not_6_out, comparator_6_gt);
  Comparator #(.Bits(6)) comparator_7 (.a(Balance), .b(6'b011001), .lt(comparator_7_lt));  // open: gt, eq
  Multiplexer #(.Bits(4)) multiplexer_8 (.sel(and_8_out), .in_0(4'b0001), .in_1(4'b0010), .out(multiplexer_8_out));
  and and_10 (and_10_out, P20_t, not_6_out);
  not not_7 (not_7_out, comparator_7_lt);
  LookUpTable #(.Bits(4)) lookuptable_3 (.in0(Pchange_t), .in1(Pnext_t), .in2(reset), .out(Idle7));
  Multiplexer #(.Bits(4)) multiplexer_9 (
    .sel(and_9_out), .in_0(multiplexer_8_out), .in_1(4'b0011), .out(multiplexer_9_out));
  and and_11 (and_11_out, Pcoffee_t, not_7_out);
  Comparator #(.Bits(6)) comparator_8 (.a(Balance), .b(6'b010100), .lt(comparator_8_lt));  // open: gt, eq
  Multiplexer #(.Bits(4)) multiplexer_10 (
    .sel(and_10_out), .in_0(multiplexer_9_out), .in_1(4'b0100), .out(multiplexer_10_out));
  not not_8 (not_8_out, comparator_8_lt);
  Multiplexer #(.Bits(4)) multiplexer_11 (
    .sel(and_11_out), .in_0(multiplexer_10_out), .in_1(4'b0101), .out(multiplexer_11_out));
  and and_12 (and_12_out, Ptea_t, not_8_out);
  Multiplexer #(.Bits(4)) multiplexer_12 (
    .sel(and_12_out), .in_0(multiplexer_11_out), .in_1(4'b0110), .out(multiplexer_12_out));
  Multiplexer #(.Bits(4)) multiplexer_13 (
    .sel(Pchange_t), .in_0(multiplexer_12_out), .in_1(4'b1111), .out(multiplexer_13_out));
  Multiplexer #(.Bits(4)) multiplexer_14 (.sel(reset), .in_0(multiplexer_13_out), .in_1(4'b0000), .out(AddCoinState));

  // Other names for the same wires on the sheet: P5raw = P5; P10raw = P10; P20raw = P20; Pchangeraw = Pchange;
  //   Pcoffeeraw = Pcoffee; Pnextraw = Pnext; Ptearaw = Ptea

  // Notes on the sheet:
  //   contents of lookuptable_1 (hex, n*v repeats v):
  //   1,1,4*0,2
  //   contents of CoinChangeTable (hex, n*v repeats v):
  //   1,9,8,8,4*c
  //   contents of lookuptable_2 (hex, n*v repeats v):
  //   1,1,0,0,0,2
  //   contents of lookuptable_3 (hex, n*v repeats v):
  //   7,f,1,1,0,0,0,a0
endmodule
