// Digital circuit Cyclic.dig as structural Verilog
module Cyclic (
  input  [3:0] In,
  output [3:0] Out
);

  wire and_2_out, and_3_out, and_4_out, and_5_out, and_6_out, and_7_out, and_8_out, not_1_out, not_2_out,
       not_3_out, not_4_out;

  not not_1 (not_1_out, In[3]);
  not not_2 (not_2_out, In[2]);
  not not_3 (not_3_out, In[1]);
  not not_4 (not_4_out, In[0]);
  and and_1 (Out[3], In[3], not_2_out, not_3_out);
  and and_2 (and_2_out, In[3], not_2_out, not_3_out);
  and and_3 (and_3_out, not_1_out, In[2]);
  and and_4 (and_4_out, not_1_out, not_2_out, In[1]);
  and and_5 (and_5_out, not_1_out, In[2], not_3_out);
  and and_6 (and_6_out, not_1_out, not_3_out, In[0]);
  and and_7 (and_7_out, not_1_out, In[1], not_4_out);
  and and_8 (and_8_out, not_2_out, not_3_out, In[0]);
  or or_1 (Out[2], and_2_out, and_3_out);
  or or_2 (Out[1], and_4_out, and_5_out);
  or or_3 (Out[0], and_6_out, and_7_out, and_8_out);
endmodule
