// Digital circuit Templatet.dig as structural Verilog
module Templatet (
  input  [3:0] In,
  input  [1:0] Selector,
  output [3:0] Output
);

  wire [3:0] _2421code_1_out, _6421code_1_out, cyclic_1_out, excess_3_1_out;

  Excess_3 excess_3_1 (.In(In), .Out(excess_3_1_out));
  Cyclic cyclic_1 (.In(In), .Out(cyclic_1_out));
  _2421code _2421code_1 (.In(In), .Out(_2421code_1_out));
  _6421code _6421code_1 (.In(In), .Out(_6421code_1_out));
  Multiplexer #(.Selector_Bits(2), .Bits(4)) multiplexer_1 (
    .sel(Selector), .in_0(excess_3_1_out), .in_1(cyclic_1_out), .in_2(_2421code_1_out),
    .in_3(_6421code_1_out), .out(Output));
endmodule
