// Digital circuit Block_A.dig as structural Verilog
module Block_A (
  input  [6:0] In,
  output C1,
  output C2,
  output C3
);

  xor xor_1 (C1, In[3], In[2], In[1], In[0]);
  xor xor_2 (C2, In[5], In[4], In[1], In[0]);
  xor xor_3 (C3, In[6], In[4], In[2], In[0]);
endmodule
