// Digital circuit Block_B.dig as structural Verilog
module Block_B (
  input  C1,
  input  C2,
  input  C3,
  output [6:0] out
);

  wire not_1_out, not_2_out, not_3_out;

  not not_1 (not_1_out, C1);
  not not_2 (not_2_out, C2);
  not not_3 (not_3_out, C3);
  and and_1 (out[6], not_1_out, not_2_out, C3);
  and and_2 (out[5], not_1_out, C2, not_3_out);
  and and_3 (out[4], not_1_out, C2, C3);
  and and_4 (out[3], C1, not_2_out, not_3_out);
  and and_5 (out[2], C1, not_2_out, C3);
  and and_6 (out[1], C1, C2, not_3_out);
  and and_7 (out[0], C1, C2, C3);
endmodule
