// Digital circuit Template.dig as structural Verilog
module Template (
  input  [6:0] In,
  output [6:0] Output
);

  wire block_a_1_c1, block_a_1_c2, block_a_1_c3;
  wire [6:0] block_b_1_out;

  Block_A block_a_1 (.In(In), .C1(block_a_1_c1), .C2(block_a_1_c2), .C3(block_a_1_c3));
  Block_B block_b_1 (.C1(block_a_1_c1), .C2(block_a_1_c2), .C3(block_a_1_c3), .out(block_b_1_out));
  assign Output = In ^ block_b_1_out;  // XOr xor_1, 7 bits wide
endmodule
