// Digital circuit test.dig as structural Verilog
module test (
  input  A,
  input  B,
  input  C,
  input  D,
  output Before,
  output After
);

  wire and_1_out, and_2_out, and_3_out, and_4_out, not_1_out, not_2_out, not_3_out;

  not not_1 (not_1_out, A);
  not not_2 (not_2_out, B);
  not not_3 (not_3_out, C);
  and and_1 (and_1_out, A, not_2_out, D);
  and and_2 (and_2_out, not_3_out, D);
  and and_3 (and_3_out, not_2_out, D);
  and and_4 (and_4_out, not_3_out, D);
  or or_1 (Before, not_1_out, and_1_out, and_2_out);
  or or_2 (After, not_1_out, and_3_out, and_4_out);
endmodule
