// Digital circuit temp.dig as structural Verilog
module temp (
  input  A,
  input  B,
  input  C,
  input  D,
  input  E,
  input  F,
  output Before,
  output After
);

  wire and_1_out, and_2_out, and_3_out, and_4_out, and_5_out, and_6_out, and_7_out, and_8_out, not_1_out,
       not_2_out, not_3_out, not_4_out, not_5_out, not_6_out, or_1_out, or_2_out;

  not not_1 (not_1_out, A);
  not not_2 (not_2_out, B);
  not not_3 (not_3_out, C);
  not not_4 (not_4_out, D);
  not not_5 (not_5_out, E);
  not not_6 (not_6_out, F);
  and and_1 (and_1_out, not_2_out, E, F);
  and and_2 (and_2_out, not_3_out, not_4_out, not_5_out);
  and and_3 (and_3_out, D, not_5_out, not_6_out);
  and and_4 (and_4_out, not_2_out, E, F);
  and and_5 (and_5_out, not_2_out, not_3_out, not_4_out, F);
  and and_6 (and_6_out, not_3_out, not_4_out, not_5_out);
  and and_7 (and_7_out, not_3_out, not_5_out, not_6_out);
  and and_8 (and_8_out, D, not_5_out, not_6_out);
  or or_1 (or_1_out, and_1_out, and_2_out, and_3_out);
  or or_2 (or_2_out, and_4_out, and_5_out, and_6_out, and_7_out, and_8_out);
  and and_9 (Before, not_1_out, or_1_out);
  and and_10 (After, not_1_out, or_2_out);
endmodule

/* Test case testcase:
A B C D E F Before After
0 0 0 0 1 1 1 1
0 0 0 0 0 1 1 1
0 0 0 0 0 1 1 1 
0 0 0 0 1 1 1 1
0 0 0 0 0 0 1 1
0 0 0 1 0 0 1 1
0 0 0 1 0 0 1 1
0 0 0 0 0 0 1 1
*/
