// Digital circuit Template.dig as structural Verilog
module Template (
  input  [3:0] In,
  output [3:0] Output
);

  wire or_1_out;
  wire [2:0] add_1_s, demultiplexer_1_out_0, demultiplexer_1_out_1, multiplexer_1_out, not_1_out;
  wire [3:0] xor_1_out;

  assign xor_1_out = 4'b1000 ^ In;  // XOr xor_1, 4 bits wide
  Demultiplexer #(.Bits(3)) demultiplexer_1 (
    .sel(In[3]), .in(In[2:0]), .out_0(demultiplexer_1_out_0), .out_1(demultiplexer_1_out_1));
  assign not_1_out = ~demultiplexer_1_out_1;  // Not not_1, 3 bits wide
  or or_1 (or_1_out, xor_1_out[0], xor_1_out[1], xor_1_out[2], xor_1_out[3]);
  Add #(.Bits(3)) add_1 (.a(not_1_out), .b(3'b001), .c_i(1'b0), .s(add_1_s));  // open: c_o
  Multiplexer #(.Bits(3)) multiplexer_1 (
    .sel(In[3]), .in_0(demultiplexer_1_out_0), .in_1(add_1_s), .out(multiplexer_1_out));
  Multiplexer #(.Bits(4)) multiplexer_2 (
    .sel(or_1_out), .in_0(4'b0000), .in_1({In[3], multiplexer_1_out}), .out(Output));
endmodule
