// Digital circuit tmp.dig as structural Verilog
module tmp (
  input  [3:0] In,
  output [3:0] Output
);

  wire [2:0] demultiplexer_1_out_0, demultiplexer_1_out_1, not_1_out, sub_1_s;

  Demultiplexer #(.Bits(3)) demultiplexer_1 (
    .sel(In[3]), .in(In[2:0]), .out_0(demultiplexer_1_out_0), .out_1(demultiplexer_1_out_1));
  assign not_1_out = ~demultiplexer_1_out_1;  // Not not_1, 3 bits wide
  Sub #(.Bits(3)) sub_1 (.a(not_1_out), .b(3'b001), .c_i(1'b0), .s(sub_1_s));  // open: c_o
  Multiplexer #(.Bits(3)) multiplexer_1 (.sel(In[3]), .in_0(demultiplexer_1_out_0), .in_1(sub_1_s), .out(Output[2:0]));

  assign Output[3] = In[3];
endmodule
