// Digital circuit Template.dig as structural Verilog
module Template (
  input  [3:0] A,
  input  [3:0] B,
  input  [2:0] S,
  input  M,
  input  C,
  output [3:0] F
);

  wire [3:0] and_1_out, and_2_out, Arithmetic, Logical, multiplexer_2_out, multiplexer_3_out, nand_1_out,
       nor_1_out, not_1_out, not_2_out, not_3_out, not_4_out, or_1_out, xnor_1_out;

  assign not_1_out = ~A;  // Not not_1, 4 bits wide
  assign not_2_out = ~B;  // Not not_2, 4 bits wide
  assign not_3_out = ~A;  // Not not_3, 4 bits wide
  assign not_4_out = ~B;  // Not not_4, 4 bits wide
  assign nand_1_out = ~(A & B);  // NAnd nand_1, 4 bits wide
  assign nor_1_out = ~(A | B);  // NOr nor_1, 4 bits wide
  assign xnor_1_out = ~(A ^ B);  // XNOr xnor_1, 4 bits wide
  assign and_1_out = B & A;  // And and_1, 4 bits wide
  assign or_1_out = B | A;  // Or or_1, 4 bits wide
  assign and_2_out = not_2_out & A;  // And and_2, 4 bits wide
  Multiplexer #(.Bits(4), .Selector_Bits(3)) multiplexer_1 (
    .sel(S), .in_0(not_1_out), .in_1(nand_1_out), .in_2(nor_1_out), .in_3(xnor_1_out), .in_4(and_1_out),
    .in_5(or_1_out), .in_6(and_2_out), .in_7(A), .out(Logical));
  Multiplexer #(.Selector_Bits(3), .Bits(4)) multiplexer_2 (
    .sel(S), .in_0(A), .in_1(A), .in_2(A), .in_3(A), .in_4(not_3_out), .in_5(4'b0000), .in_6({A[2:0], 1'b0}),
    .in_7({1'b0, A[3:1]}), .out(multiplexer_2_out));
  Multiplexer #(.Selector_Bits(3), .Bits(4)) multiplexer_3 (
    .sel(S), .in_0(4'b0000), .in_1(4'b1111), .in_2(B), .in_3(not_4_out), .in_4(4'b0000), .in_5(B),
    .in_6(4'b0000), .in_7(4'b0000), .out(multiplexer_3_out));
  Add #(.Bits(4)) add_1 (.a(multiplexer_2_out), .b(multiplexer_3_out), .c_i(C), .s(Arithmetic));  // open: c_o
  Multiplexer #(.Bits(4)) multiplexer_4 (.sel(M), .in_0(Logical), .in_1(Arithmetic), .out(F));
endmodule
