// Digital circuit Template.dig as structural Verilog
module Template (
  input  P,
  input  T,
  input  D,
  input  C,
  input  B,
  input  A,
  input  Clr,
  input  Load,
  input  Clock,
  output QD,
  output QC,
  output QB,
  output QA,
  output RCO
);

  wire and_1_out, and_2_out, and_3_out;

  and and_1 (and_1_out, P, T);
  T_FF t_ff_1 (.T(and_1_out), .C(Clock), .Q(QA));  // open: nQ
  T_FF t_ff_2 (.T(QA), .C(Clock), .Q(QB));  // open: nQ
  and and_2 (and_2_out, QB, QA);
  T_FF t_ff_3 (.T(and_2_out), .C(Clock), .Q(QC));  // open: nQ
  and and_3 (and_3_out, QA, QB, QC);
  T_FF t_ff_4 (.T(and_3_out), .C(Clock), .Q(QD));  // open: nQ
  and and_4 (RCO, QA, QB, QC, QD);
endmodule
