// Digital circuit sol.dig as structural Verilog
module sol (
  input  P,
  input  T,
  input  D,
  input  C,
  input  B,
  input  A,
  input  Clr,
  input  Load,
  input  Clock,
  output QD,
  output QC,
  output QB,
  output QA,
  output RCO
);

  wire and_1_out;
  wire [1:0] lookuptable_1_out;
  wire [3:0] add_1_s, multiplexer_1_out;

  and and_1 (and_1_out, P, T);
  LookUpTable #(.Bits(2)) lookuptable_1 (.in0(Clr), .in1(Load), .in2(and_1_out), .out(lookuptable_1_out));
  Multiplexer #(.Bits(4), .Selector_Bits(2)) multiplexer_1 (
    .sel(lookuptable_1_out), .in_0({QD, QC, QB, QA}), .in_1(4'b0000), .in_2({D, C, B, A}), .in_3(add_1_s),
    .out(multiplexer_1_out));
  D_FF_AS #(.Bits(4)) d_ff_as_1 (
    .Set(1'b0), .D(multiplexer_1_out), .C(Clock), .Clr(1'b0), .Q({QD, QC, QB, QA}));  // open: nQ
  Add #(.Bits(4)) add_1 (.a({QD, QC, QB, QA}), .b(4'b0000), .c_i(1'b1), .s(add_1_s));  // open: c_o
  and and_2 (RCO, QA, QB, QC, QD);

  // Notes on the sheet:
  //   contents of lookuptable_1 (hex, n*v repeats v):
  //   2,2,1,0,2,2,1,3
endmodule

/* Test case T1:
P T D C B A \Clr \Load Clock QD QC QB QA RCO
0 0 x x x x 0 1 0 x x x x x
0 0 x x x x 0 1 1 0 0 0 0 0
x x 1 1 0 1 1 0 0 0 0 0 0 0
x x 1 1 0 1 1 0 1 1 1 0 1 0
x x 1 1 0 1 1 0 0 1 1 0 1 0
x x 1 1 0 1 1 0 1 1 1 0 1 0 
1 1 x x x x 1 1 0 1 1 0 1 0
1 1 x x x x 1 1 1 1 1 1 0 0
1 1 x x x x 1 1 0 1 1 1 0 0
1 1 x x x x 1 1 1 1 1 1 1 1
1 1 x x x x 1 1 0 1 1 1 1 1
1 1 x x x x 1 1 1 0 0 0 0 0
1 1 x x x x 1 1 0 0 0 0 0 0
1 1 x x x x 1 1 1 0 0 0 1 0
1 1 x x x x 1 1 0 0 0 0 1 0
1 1 x x x x 1 1 1 0 0 1 0 0
x x x x x x 0 1 0 0 0 1 0 0
x x x x x x 0 1 1 0 0 0 0 0
1 1 x x x x 1 1 0 0 0 0 0 0
1 1 x x x x 1 1 1 0 0 0 1 0
1 0 x x x x 1 1 0 0 0 0 1 0
1 0 x x x x 1 1 1 0 0 0 1 0
*/
