// Digital circuit test.dig as structural Verilog
module test (
  input  P,
  input  T,
  input  D,
  input  C,
  input  B,
  input  A,
  input  Clr,
  input  Load,
  input  Clock,
  output QA
);

  wire and_1_out, not_1_out;

  and and_1 (and_1_out, A, not_1_out);
  not not_1 (not_1_out, Load);
  D_FF_AS d_ff_as_1 (.Set(1'b0), .D(and_1_out), .C(Clock), .Clr(Clr), .Q(QA));  // open: nQ
endmodule
