// Digital circuit mysol.dig as structural Verilog
module mysol (
  input  A,
  input  B,
  input  Clr,
  input  Clock,
  output state,
  output Z
);

  wire lookuptable_1_out, lookuptable_2_out, lookuptable_3_out, multiplexer_1_out, not_1_out;

  not not_1 (not_1_out, Clr);
  LookUpTable lookuptable_1 (.in0(A), .in1(B), .out(lookuptable_1_out));
  LookUpTable lookuptable_2 (.in0(A), .in1(B), .out(lookuptable_2_out));
  D_FF_AS d_ff_as_1 (.Set(1'b0), .D(multiplexer_1_out), .C(Clock), .Clr(not_1_out), .Q(state));  // open: nQ
  Multiplexer multiplexer_1 (.sel(state), .in_0(lookuptable_1_out), .in_1(lookuptable_2_out), .out(multiplexer_1_out));
  LookUpTable lookuptable_3 (.in0(A), .in1(B), .in2(state), .out(lookuptable_3_out));
  and and_1 (Z, lookuptable_3_out, ~not_1_out);  // And

  // Notes on the sheet:
  //   contents of lookuptable_1 (hex, n*v repeats v):
  //   0,0,0,1
  //   contents of lookuptable_2 (hex, n*v repeats v):
  //   0,1,1,1
  //   contents of lookuptable_3 (hex, n*v repeats v):
  //   0,1,1,0,1,0,0,1
endmodule
