// Digital circuit sol.dig as structural Verilog
module sol (
  input  P,
  input  Clr,
  input  clock,
  output Z
);

  wire d_ff_1_q, d_ff_2_q, d_ff_as_1_q, lookuptable_1_out, lookuptable_2_out, lookuptable_3_out,
       multiplexer_1_out;

  D_FF d_ff_1 (.D(P), .C(clock), .Q(d_ff_1_q));  // open: nQ
  D_FF d_ff_2 (.D(d_ff_1_q), .C(clock), .Q(d_ff_2_q));  // open: nQ
  LookUpTable lookuptable_1 (.in0(d_ff_2_q), .in1(1'b0), .out(lookuptable_1_out));
  LookUpTable lookuptable_2 (.in0(d_ff_2_q), .in1(1'b0), .out(lookuptable_2_out));
  Multiplexer multiplexer_1 (
    .sel(d_ff_as_1_q), .in_0(lookuptable_1_out), .in_1(lookuptable_2_out), .out(multiplexer_1_out));
  D_FF_AS d_ff_as_1 (.Set(1'b0), .D(multiplexer_1_out), .C(clock), .Clr(Clr), .Q(d_ff_as_1_q));  // open: nQ
  LookUpTable lookuptable_3 (.in0(d_ff_2_q), .in1(d_ff_as_1_q), .out(lookuptable_3_out));
  and and_1 (Z, lookuptable_3_out, ~Clr);  // And

  // Notes on the sheet:
  //   contents of lookuptable_1 (hex, n*v repeats v):
  //   0,1
  //   contents of lookuptable_2 (hex, n*v repeats v):
  //   0,1
  //   contents of lookuptable_3 (hex, n*v repeats v):
  //   0,1
endmodule
