// Digital circuit DflipFlop.dig as structural Verilog
module DflipFlop (
  input  P,
  input  Clr,
  input  clock,
  output [1:0] state,
  output Z
);

  wire [1:0] lookuptable_1_out, lookuptable_2_out, lookuptable_3_out, multiplexer_1_out;

  LookUpTable #(.Bits(2)) lookuptable_1 (.in0(P), .in1(1'b0), .out(lookuptable_1_out));
  LookUpTable #(.Bits(2)) lookuptable_2 (.in0(P), .in1(1'b0), .out(lookuptable_2_out));
  LookUpTable #(.Bits(2)) lookuptable_3 (.in0(P), .in1(1'b0), .out(lookuptable_3_out));
  Multiplexer #(.Bits(2), .Selector_Bits(2)) multiplexer_1 (
    .sel(state), .in_0(lookuptable_1_out), .in_1(lookuptable_2_out), .in_2(lookuptable_3_out), .in_3(2'b00),
    .out(multiplexer_1_out));
  D_FF_AS #(.Bits(2)) d_ff_as_1 (.Set(1'b0), .D(multiplexer_1_out), .C(clock), .Clr(Clr), .Q(state));  // open: nQ
  LookUpTable lookuptable_4 (.in0(state[0]), .in1(state[1]), .out(Z));

  // Notes on the sheet:
  //   contents of lookuptable_1 (hex, n*v repeats v):
  //   0,1
  //   contents of lookuptable_2 (hex, n*v repeats v):
  //   0,2
  //   contents of lookuptable_3 (hex, n*v repeats v):
  //   0,2
  //   contents of lookuptable_4 (hex, n*v repeats v):
  //   0,1
endmodule
