// Digital circuit jk.dig as structural Verilog
module jk (
  input  J,
  input  K,
  input  clk,
  output Q,
  output Q_2,
  output out_5,
  output out_7
);

  wire and_1_out, and_2_out;

  and and_1 (and_1_out, Q, clk, J);
  and and_2 (and_2_out, K, clk, Q_2);
  JK_FF jk_ff_1 (.J(J), .C(clk), .K(K), .Q(out_5), .nQ(out_7));
  nor nor_1 (Q, and_1_out, Q_2);
  nor nor_2 (Q_2, Q, and_2_out);
endmodule
