// Digital circuit mysol.dig as structural Verilog
module mysol (
  input  P,
  input  Clr,
  input  clock,
  output Z
);

  wire and_1_out, and_2_out, d_ff_as_1_q, d_ff_as_2_q, not_1_out, not_2_out, or_1_out;

  not not_1 (not_1_out, d_ff_as_1_q);
  and and_1 (and_1_out, not_1_out, P, Z);
  and and_2 (and_2_out, d_ff_as_1_q, P);
  or or_1 (or_1_out, and_1_out, and_2_out);
  D_FF_AS d_ff_as_1 (.Set(1'b0), .D(or_1_out), .C(clock), .Clr(Clr), .Q(d_ff_as_1_q));  // open: nQ
  D_FF_AS d_ff_as_2 (.Set(1'b0), .D(P), .C(clock), .Clr(Clr), .Q(d_ff_as_2_q));  // open: nQ
  and and_3 (Z, not_2_out, d_ff_as_2_q);
  not not_2 (not_2_out, d_ff_as_1_q);
endmodule
