// Digital circuit sol.dig as structural Verilog
module sol (
  input  P,
  input  Clr,
  input  clock,
  output Z
);

  wire and_1_out, and_2_out, and_3_out, and_4_out, d_ff_1_nq, d_ff_2_q, or_1_out;

  and and_1 (and_1_out, ~d_ff_2_q, P, d_ff_1_nq, ~Clr);  // And
  and and_2 (and_2_out, P, Z);
  and and_3 (and_3_out, P, d_ff_2_q);
  or or_1 (or_1_out, and_2_out, and_3_out);
  and and_4 (and_4_out, ~Clr, or_1_out);  // And
  D_FF d_ff_1 (.D(and_1_out), .C(clock), .Q(Z), .nQ(d_ff_1_nq));
  D_FF d_ff_2 (.D(and_4_out), .C(clock), .Q(d_ff_2_q));  // open: nQ
endmodule

/* Test case T1:
\Clr P clock Z
1 0 0 x
1 0 1 0
0 0 0 0
0 0 1 0
0 1 0 0
0 1 1 1
0 1 0 1
0 1 1 0
0 1 0 0
0 1 1 0
0 0 0 0
0 0 1 0
0 1 0 0
0 1 1 1
0 0 0 1
0 0 1 0
*/
