// Digital circuit final01.dig as structural Verilog
module final01 (
  input  clock,
  input  [7:0] A,
  input  [7:0] B,
  input  Add,
  input  reset,
  output [11:0] \output 
);

  wire Add_t, and_1_out, d_ff_3_nq;
  wire [1:0] multiplexer_3_out, multiplexer_4_out, multiplexer_5_out, state;
  wire [8:0] add_1_s;
  wire [11:0] add_2_s, add_3_s, add_t_t, multiplexer_1_out, multiplexer_2_out;

  Add #(.Bits(8)) add_1 (.a(A), .b(B), .c_i(1'b0), .s(add_1_s[7:0]), .c_o(add_1_s[8]));
  Add #(.Bits(12)) add_2 (.a(add_t_t), .b({12{1'b0}}), .c_i(1'b1), .s(add_2_s));  // open: c_o
  Add #(.Bits(12)) add_3 (.a(add_t_t), .b({3'b000, add_1_s}), .c_i(1'b0), .s(add_3_s));  // open: c_o
  Multiplexer #(.Selector_Bits(2), .Bits(12)) multiplexer_1 (
    .sel(state), .in_0({12{1'b0}}), .in_1(add_t_t), .in_2(add_2_s), .in_3(add_t_t), .out(multiplexer_1_out));
  Multiplexer #(.Selector_Bits(2), .Bits(12)) multiplexer_2 (
    .sel(state), .in_0({12{1'b0}}), .in_1(add_3_s), .in_2(\output ), .in_3(\output ), .out(multiplexer_2_out));
  D_FF #(.Bits(12)) d_ff_1 (.D(multiplexer_1_out), .C(clock), .Q(add_t_t));  // open: nQ
  D_FF #(.Bits(12)) d_ff_2 (.D(multiplexer_2_out), .C(clock), .Q(\output ));  // open: nQ
  D_FF d_ff_3 (.D(Add), .C(clock), .nQ(d_ff_3_nq));  // open: Q
  and and_1 (and_1_out, d_ff_3_nq, Add);
  Multiplexer #(.Bits(2)) multiplexer_3 (.sel(Add_t), .in_0(2'b01), .in_1(2'b10), .out(multiplexer_3_out));
  Multiplexer #(.Bits(2)) multiplexer_4 (.sel(reset), .in_0(multiplexer_3_out), .in_1(2'b00), .out(multiplexer_4_out));
  D_FF d_ff_4 (.D(and_1_out), .C(clock), .Q(Add_t));  // open: nQ
  Multiplexer #(.Bits(2), .Selector_Bits(2)) multiplexer_5 (
    .sel(state), .in_0(2'b01), .in_1(multiplexer_4_out), .in_2(2'b01), .in_3(2'b00), .out(multiplexer_5_out));
  D_FF #(.Bits(2)) d_ff_5 (.D(multiplexer_5_out), .C(clock), .Q(state));  // open: nQ
  Seven_Seg_Hex seven_seg_hex_1 (.d(\output [11:8]), .dp(1'b0));
  Seven_Seg_Hex seven_seg_hex_2 (.d(\output [7:4]), .dp(1'b0));
  Seven_Seg_Hex seven_seg_hex_3 (.d(\output [3:0]), .dp(1'b0));

  // Other names for the same wires on the sheet: Addraw = Add; clk = clock
endmodule
