// Digital circuit D_FilpFlop.dig as structural Verilog
module D_FilpFlop (
  input  D,
  output Q,
  output Q_2
);

  wire not_1_out;

  not not_1 (not_1_out, D);
  nor nor_1 (Q, not_1_out, Q_2);
  nor nor_2 (Q_2, Q, D);
endmodule
