// Digital circuit RS_Clock.dig as structural Verilog
module RS_Clock (
  input  in_1,
  input  in_2,
  input  clk,
  output Q,
  output Q_2
);

  wire and_1_out, and_2_out;

  and and_1 (and_1_out, in_1, clk);
  and and_2 (and_2_out, clk, in_2);
  nor nor_1 (Q, and_1_out, Q_2);
  nor nor_2 (Q_2, Q, and_2_out);
endmodule
