// Digital circuit 04_Template.dig as structural Verilog
module _04_Template (
  input  C1,
  input  C2,
  output Z
);

  and and_1 (Z, C1, C2);

  // Notes on the sheet:
  //   C1: Hz: 2
  //   C2: Hz: 3
endmodule
