// Digital circuit Template.dig as structural Verilog
module Template (
  input  A,
  input  B,
  input  Cin,
  output Sum__SOP,
  output Cout__SOP,
  output Cout__POS,
  output Sum__POS
);

  wire and_1_out, and_2_out, and_3_out, and_4_out, and_5_out, and_6_out, and_7_out, not_1_out, not_2_out,
       not_3_out, or_1_out, or_2_out, or_3_out, or_4_out, or_5_out, or_6_out, or_7_out;

  not not_1 (not_1_out, A);
  not not_2 (not_2_out, B);
  not not_3 (not_3_out, Cin);
  and and_1 (and_1_out, A, Cin);
  and and_2 (and_2_out, B, Cin);
  and and_3 (and_3_out, A, B);
  and and_4 (and_4_out, not_1_out, not_2_out, Cin);
  and and_5 (and_5_out, A, not_2_out, not_3_out);
  and and_6 (and_6_out, A, B, Cin);
  and and_7 (and_7_out, not_1_out, B, not_3_out);
  or or_1 (or_1_out, A, B);
  or or_2 (or_2_out, B, Cin);
  or or_3 (or_3_out, A, Cin);
  or or_4 (or_4_out, A, B, Cin);
  or or_5 (or_5_out, not_1_out, not_2_out, Cin);
  or or_6 (or_6_out, not_1_out, B, not_3_out);
  or or_7 (or_7_out, A, not_2_out, not_3_out);
  and and_8 (Cout__POS, or_1_out, or_2_out, or_3_out);
  and and_9 (Sum__POS, or_4_out, or_5_out, or_6_out, or_7_out);
  or or_8 (Cout__SOP, and_1_out, and_2_out, and_3_out);
  or or_9 (Sum__SOP, and_4_out, and_5_out, and_6_out, and_7_out);
endmodule
