// Digital circuit Template.dig as structural Verilog
module Template (
  input  A,
  input  B,
  input  C,
  input  D,
  output Z1_SOP,
  output Z2_SOP,
  output Z3_SOP,
  output Z1_POS,
  output Z2_POS,
  output Z3_POS
);

  wire and_1_out, and_2_out, and_3_out, and_4_out, and_5_out, and_6_out, and_7_out, and_8_out, and_9_out,
       and_10_out, and_11_out, and_12_out, not_1_out, not_2_out, not_3_out, not_4_out, or_1_out, or_2_out,
       or_3_out, or_4_out, or_5_out, or_6_out, or_7_out, or_8_out, or_9_out, or_10_out, or_11_out, or_12_out,
       or_13_out, or_14_out;

  not not_1 (not_1_out, A);
  not not_2 (not_2_out, B);
  not not_3 (not_3_out, C);
  not not_4 (not_4_out, D);
  or or_1 (or_1_out, A, B);
  or or_2 (or_2_out, not_3_out, not_4_out);
  or or_3 (or_3_out, B, not_3_out);
  or or_4 (or_4_out, A, not_3_out);
  or or_5 (or_5_out, A, not_4_out);
  or or_6 (or_6_out, C, D);
  or or_7 (or_7_out, not_1_out, not_2_out);
  or or_8 (or_8_out, not_1_out, D);
  or or_9 (or_9_out, not_1_out, C);
  or or_10 (or_10_out, not_2_out, C);
  or or_11 (or_11_out, not_1_out, C);
  or or_12 (or_12_out, not_2_out, D);
  or or_13 (or_13_out, B, not_4_out);
  or or_14 (or_14_out, A, not_3_out);
  and and_1 (and_1_out, A, not_3_out, not_4_out);
  and and_2 (and_2_out, A, B, not_4_out);
  and and_3 (and_3_out, B, not_3_out, not_4_out);
  and and_4 (and_4_out, A, not_3_out, D);
  and and_5 (and_5_out, not_1_out, not_2_out, C);
  and and_6 (and_6_out, not_1_out, not_2_out, D);
  and and_7 (and_7_out, not_2_out, C, D);
  and and_8 (and_8_out, not_1_out, B, C);
  and and_9 (and_9_out, not_1_out, not_2_out, not_3_out, not_4_out);
  and and_10 (and_10_out, A, not_2_out, C, not_4_out);
  and and_11 (and_11_out, A, B, C, D);
  and and_12 (and_12_out, not_1_out, B, not_3_out, D);
  and and_13 (Z1_POS, or_1_out, or_2_out, or_3_out, or_4_out, or_5_out);
  and and_14 (Z2_POS, or_6_out, or_7_out, or_8_out, or_9_out, or_10_out);
  and and_15 (Z3_POS, or_11_out, or_12_out, or_13_out, or_14_out);
  or or_15 (Z1_SOP, and_1_out, and_2_out, and_3_out, and_4_out);
  or or_16 (Z2_SOP, and_5_out, and_6_out, and_7_out, and_8_out);
  or or_17 (Z3_SOP, and_9_out, and_10_out, and_11_out, and_12_out);
endmodule
