// Digital circuit Template.dig as structural Verilog
module Template (
  input  X0,
  input  X1,
  input  Selector,
  output Z_SOP,
  output Z_POS
);

  wire and_1_out, and_2_out, not_1_out, not_2_out, not_3_out, or_1_out, or_2_out;

  not not_1 (not_1_out, X0);
  not not_2 (not_2_out, X1);
  not not_3 (not_3_out, Selector);
  and and_1 (and_1_out, X0, not_3_out);
  and and_2 (and_2_out, X1, Selector);
  or or_1 (or_1_out, X0, Selector);
  or or_2 (or_2_out, X1, not_3_out);
  and and_3 (Z_POS, or_1_out, or_2_out);
  or or_3 (Z_SOP, and_1_out, and_2_out);
endmodule
