// Digital circuit another_sol.dig as structural Verilog
module another_sol (
  input  clock,
  input  [8:0] N,
  input  start,
  input  reset,
  output [7:0] displayout,
  output valid,
  output [3:0] state,
  output done,
  output [31:0] clockcount
);

  wire clk, comparator_1_eq, comparator_2_eq, comparator_3_eq, comparator_4_eq, comparator_5_eq,
       comparator_6_eq, comparator_7_eq, comparator_8_eq, comparator_9_gt, multiplexer_1_out, not_1_out,
       not_2_out, state2_lt, state9_lt;
  wire [3:0] _2loop, getinput, multiplexer_8_out, multiplexer_9_out, multiplexer_10_out, multiplexer_11_out,
       multiplexer_14_out;
  wire [7:0] multiplexer_2_out, multiplexer_3_out, multiplexer_7_out, rom_1_d;
  wire [8:0] add_1_s, add_3_s, cnt, j, multiplexer_5_out, multiplexer_6_out;
  wire [9:0] add_2_s, i, multiplexer_4_out, MX;

  Comparator #(.Bits(4)) comparator_1 (.a(state), .b(4'b0011), .eq(comparator_1_eq));  // open: gt, lt
  Comparator #(.Bits(4)) comparator_2 (.a(state), .b(4'b1000), .eq(comparator_2_eq));  // open: gt, lt
  Multiplexer multiplexer_1 (.sel(comparator_1_eq), .in_0(1'b0), .in_1(1'b1), .out(multiplexer_1_out));
  Comparator #(.Bits(4)) comparator_3 (.a(state), .b(4'b1010), .eq(comparator_3_eq));  // open: gt, lt
  ROM #(.AddrBits(9), .Bits(8), .isProgramMemory("true")) rom_1 (.A(i[8:0]), .sel(multiplexer_1_out), .D(rom_1_d));
  Comparator #(.Bits(4)) comparator_4 (.a(state), .b(4'b0011), .eq(comparator_4_eq));  // open: gt, lt
  Multiplexer #(.Bits(8)) multiplexer_2 (.sel(comparator_4_eq), .in_0(i[7:0]), .in_1(rom_1_d), .out(multiplexer_2_out));
  D_FF d_ff_1 (.D(comparator_3_eq), .C(clk), .Q(valid));  // open: nQ
  RAMDualPort #(.AddrBits(8), .Bits(9)) u_Cnt (
    .A(multiplexer_2_out), .Din(add_1_s), .str(comparator_1_eq), .C(clk), .ld(1'b1), .D(cnt));
  Add #(.Bits(9)) add_1 (.a(cnt), .b({9{1'b0}}), .c_i(1'b1), .s(add_1_s));  // open: c_o
  Add #(.Bits(10)) add_2 (.a(i), .b({10{1'b0}}), .c_i(1'b1), .s(add_2_s));  // open: c_o
  Comparator #(.Bits(4)) comparator_5 (.a(state), .b(4'b0000), .eq(comparator_5_eq));  // open: gt, lt
  Comparator #(.Bits(4)) comparator_6 (.a(state), .b(4'b1000), .eq(comparator_6_eq));  // open: gt, lt
  Add #(.Bits(9)) add_3 (.a(j), .b({9{1'b0}}), .c_i(1'b1), .s(add_3_s));  // open: c_o
  Multiplexer #(.Bits(8)) multiplexer_3 (
    .sel(comparator_5_eq), .in_0(displayout), .in_1({8{1'b0}}), .out(multiplexer_3_out));
  Comparator #(.Bits(4)) comparator_7 (.a(state), .b(4'b1000), .eq(comparator_7_eq));  // open: gt, lt
  Multiplexer #(.Bits(10), .Selector_Bits(4)) multiplexer_4 (
    .sel(state), .in_0({10{1'b0}}), .in_1({10{1'b0}}), .in_2(i), .in_3(add_2_s), .in_4(i), .in_5(i),
    .in_6({10{1'b0}}), .in_7(i), .in_8(i), .in_9(i), .in_10(i), .in_11(i), .in_12(add_2_s), .in_13(i),
    .in_14(i), .in_15(i), .out(multiplexer_4_out));
  Multiplexer #(.Bits(9)) multiplexer_5 (.sel(comparator_6_eq), .in_0(j), .in_1({9{1'b0}}), .out(multiplexer_5_out));
  Multiplexer #(.Bits(9)) multiplexer_6 (
    .sel(comparator_8_eq), .in_0(multiplexer_5_out), .in_1(add_3_s), .out(multiplexer_6_out));
  Comparator #(.Bits(4)) comparator_8 (.a(state), .b(4'b1010), .eq(comparator_8_eq));  // open: gt, lt
  Multiplexer #(.Bits(8)) multiplexer_7 (
    .sel(comparator_7_eq), .in_0(multiplexer_3_out), .in_1(i[7:0]), .out(multiplexer_7_out));
  D_FF #(.Bits(10)) d_ff_2 (.D(multiplexer_4_out), .C(clk), .Q(i));  // open: nQ
  D_FF #(.Bits(8)) d_ff_3 (.D(multiplexer_7_out), .C(clk), .Q(displayout));  // open: nQ
  D_FF #(.Bits(9)) d_ff_4 (.D(multiplexer_6_out), .C(clk), .Q(j));  // open: nQ
  Register #(.Bits(10)) register_1 (.D(10'hff), .C(clk), .en(1'b1), .Q(MX));
  and and_1 (clk, clock, start);
  Comparator #(.Bits(9)) state9 (.a(j), .b(cnt), .lt(state9_lt));  // open: gt, eq
  Multiplexer #(.Bits(4)) multiplexer_8 (.sel(state2_lt), .in_0(4'b0110), .in_1(4'b0011), .out(multiplexer_8_out));
  Comparator #(.Bits(9)) state2 (.a(i[8:0]), .b(N), .lt(state2_lt));  // open: gt, eq
  Multiplexer #(.Bits(4)) multiplexer_9 (.sel(state9_lt), .in_0(4'b1100), .in_1(4'b1010), .out(multiplexer_9_out));
  Multiplexer #(.Bits(4)) multiplexer_10 (.sel(reset), .in_0(4'b1101), .in_1(4'b0000), .out(multiplexer_10_out));
  Comparator #(.Bits(10)) comparator_9 (.a(i), .b(MX), .gt(comparator_9_gt));  // open: eq, lt
  D_FF #(.Bits(4)) d_ff_5 (.D(multiplexer_14_out), .C(clk), .Q(state));  // open: nQ
  Multiplexer #(.Bits(4)) multiplexer_11 (.sel(start), .in_0(4'b0000), .in_1(4'b0001), .out(multiplexer_11_out));
  not not_1 (not_1_out, comparator_9_gt);
  Multiplexer #(.Bits(4)) multiplexer_12 (.sel(reset), .in_0(multiplexer_11_out), .in_1(4'b0000), .out(getinput));
  Multiplexer #(.Bits(4)) multiplexer_13 (.sel(not_1_out), .in_0(4'b1101), .in_1(4'b1000), .out(_2loop));
  Multiplexer #(.Bits(4), .Selector_Bits(4)) multiplexer_14 (
    .sel(state), .in_0(getinput), .in_1(4'b0010), .in_2(multiplexer_8_out), .in_3(4'b0010), .in_4(state),
    .in_5(state), .in_6(4'b0111), .in_7(_2loop), .in_8(4'b1001), .in_9(multiplexer_9_out), .in_10(4'b1001),
    .in_11(state), .in_12(4'b0111), .in_13(multiplexer_10_out), .in_14(state), .in_15(state),
    .out(multiplexer_14_out));
  not not_2 (not_2_out, done);
  Comparator #(.Bits(4)) comparator_10 (.a(state), .b(4'b1101), .eq(done));  // open: gt, lt
  Counter #(.Bits(32)) counter_1 (.en(not_2_out), .C(clk), .clr(reset), .out(clockcount));  // open: ovf

  // Other names for the same wires on the sheet: displayoutput[7:0] = displayout

  // Notes on the sheet:
  //   clock: Hz: 10
  //   contents of rom_1 (hex, n*v repeats v):
  //   1,0,0,3,1,6
endmodule
