// Digital circuit jo_final.dig as structural Verilog
module jo_final (
  input  [8:0] N,
  input  reset,
  input  start,
  input  clock,
  output [7:0] addr,
  output [8:0] cnt,
  output [7:0] k_th_num,
  output valid,
  output [8:0] j,
  output [31:0] clockcount,
  output [7:0] displayout,
  output [7:0] reRamA,
  output done
);

  wire and_2_out, and_3_out, and_4_out, and_5_out, clk, comparator_1_lt, comparator_2_lt, comparator_3_lt,
       comparator_4_lt, comparator_5_gt, comparator_6_lt, iinc, isResetRam, isWrite, not_1_out, or_3_out;
  wire [7:0] counter_1_out, multiplexer_3_out, ROMFILE_d;
  wire [8:0] add_1_s, counter_3_out, counter_6_out, multiplexer_1_out;

  Comparator #(.Bits(8)) comparator_1 (.a(counter_1_out), .b({8{1'b1}}), .lt(comparator_1_lt));  // open: gt, eq
  and and_1 (isResetRam, comparator_1_lt, reset);
  Comparator #(.Bits(8)) comparator_2 (.a(k_th_num), .b({8{1'b1}}), .lt(comparator_2_lt));  // open: gt, eq
  Comparator #(.Bits(9)) comparator_3 (.a(counter_3_out), .b(N), .lt(comparator_3_lt));  // open: gt, eq
  and and_2 (and_2_out, clock, start);
  and and_3 (and_3_out, reset, clock);
  and and_4 (and_4_out, comparator_2_lt, ~isWrite, iinc);  // And
  Counter #(.Bits(8)) counter_1 (.en(isResetRam), .C(clk), .clr(start), .out(counter_1_out));  // open: ovf
  or or_1 (clk, and_2_out, and_3_out);
  Counter #(.Bits(8)) counter_2 (.en(and_4_out), .C(clk), .clr(reset), .out(k_th_num));  // open: ovf
  Counter #(.Bits(9)) counter_3 (.en(comparator_3_lt), .C(clk), .clr(reset), .out(counter_3_out));  // open: ovf
  D_FF #(.Bits(8)) d_ff_1 (.D(counter_1_out), .C(clk), .Q(reRamA));  // open: nQ
  Comparator #(.Bits(9)) comparator_4 (.a(counter_3_out), .b(N), .lt(comparator_4_lt));  // open: gt, eq
  and and_5 (and_5_out, start, comparator_4_lt);
  ROM #(.AddrBits(9), .isProgramMemory("true"), .Bits(8)) ROMFILE (.A(counter_3_out), .sel(and_5_out), .D(ROMFILE_d));
  Multiplexer #(.Bits(9)) multiplexer_1 (.sel(isResetRam), .in_0(add_1_s), .in_1({9{1'b0}}), .out(multiplexer_1_out));
  or or_2 (isWrite, isResetRam, and_5_out);
  Multiplexer #(.Bits(8)) multiplexer_2 (.sel(isWrite), .in_0(k_th_num), .in_1(ROMFILE_d), .out(addr));
  not not_1 (not_1_out, done);
  Multiplexer #(.Bits(8)) multiplexer_3 (.sel(isResetRam), .in_0(addr), .in_1(reRamA), .out(multiplexer_3_out));
  Add #(.Bits(9)) add_1 (.a(cnt), .b({9{1'b0}}), .c_i(1'b1), .s(add_1_s));  // open: c_o
  Counter #(.Bits(32)) counter_4 (.en(not_1_out), .C(clk), .clr(reset), .out(clockcount));  // open: ovf
  RAMDualPort #(.AddrBits(8), .Bits(9)) Count (
    .A(multiplexer_3_out), .Din(multiplexer_1_out), .str(isWrite), .C(clk), .ld(1'b1), .D(cnt));
  Seven_Seg_Hex seven_seg_hex_1 (.d(addr[7:4]), .dp(1'b0));
  or or_3 (or_3_out, reset, iinc);
  Seven_Seg_Hex seven_seg_hex_2 (.d(addr[3:0]), .dp(1'b0));
  Counter #(.Bits(9)) counter_5 (.en(valid), .C(clk), .clr(or_3_out), .out(j));  // open: ovf
  Comparator #(.Bits(9)) comparator_5 (.a(cnt), .b(j), .gt(comparator_5_gt));  // open: eq, lt
  Counter #(.Bits(9)) counter_6 (.en(valid), .C(clk), .clr(reset), .out(counter_6_out));  // open: ovf
  not not_2 (iinc, comparator_5_gt);
  and and_6 (valid, comparator_5_gt, ~isWrite);  // And
  Comparator #(.Bits(9)) comparator_6 (.a(counter_6_out), .b(N), .eq(done), .lt(comparator_6_lt));  // open: gt
  RAMDualPort #(.AddrBits(9), .Bits(8)) ramdualport_1 (
    .A(counter_6_out), .Din(addr), .str(comparator_6_lt), .C(clk), .ld(1'b0));  // open: D

  assign displayout = addr;

  // Notes on the sheet:
  //   contents of ROMFILE (hex, n*v repeats v):
  //   1,2,1,0,3,2,0,1,3,2,0,1,3,2,0,1,3,2,0,1,3,2,0,1,3,2,0,1,3,2,0
  //   ,1,13*0,1,16*0,1,1,14*0,1,13*0,1
endmodule

/* Test case FINALT1:
clock N reset start valid displayout done clockcount
            program(3,2,0,1,3,2,0,1,3,2,0,1,3,2,0,1,3,2,0,1,3,2,0,1,3,2,0,1)
0 28 0 0 X X X X
1 28 0 0 X X X X
0 28 1 0 X X X X
1 28 1 0 X X X X
0 28 0 1 X X X X
1 28 0 1 X X X X
repeat (1000000) C 28 0 1 X X X X
1 28 0 1 X X X 0xBAADBEEF
*/
