// Digital circuit loop_1.dig as structural Verilog
module loop_1 (
  input  clk,
  input  reset,
  output [3:0] out_3
);

  wire comparator_1_gt, not_1_out;
  wire [1:0] ifin, multiplexer_1_out, multiplexer_3_out, state;
  wire [3:0] add_1_s, multiplexer_2_out;

  CounterPreset counterpreset_1 ();  // open: en, C, dir, in, ld, clr, out, ovf
  Add #(.Bits(4)) add_1 (.a(out_3), .b(4'b0001), .c_i(1'b0), .s(add_1_s));  // open: c_o
  D_FF #(.Bits(2)) d_ff_1 (.D(multiplexer_1_out), .C(clk), .Q(state));  // open: nQ
  Multiplexer #(.Bits(2), .Selector_Bits(2)) multiplexer_1 (
    .sel(state), .in_0(2'b01), .in_1(ifin), .in_2(2'b01), .in_3(2'b00), .out(multiplexer_1_out));
  Multiplexer #(.Bits(4), .Selector_Bits(2)) multiplexer_2 (
    .sel(state), .in_0(4'b0000), .in_1(out_3), .in_2(add_1_s), .in_3(out_3), .out(multiplexer_2_out));
  D_FF #(.Bits(4)) d_ff_2 (.D(multiplexer_2_out), .C(clk), .Q(out_3));  // open: nQ
  Comparator #(.Bits(4)) comparator_1 (.a(out_3), .b(4'b1010), .gt(comparator_1_gt));  // open: eq, lt
  not not_1 (not_1_out, comparator_1_gt);
  Multiplexer #(.Bits(2)) multiplexer_3 (.sel(not_1_out), .in_0(2'b01), .in_1(2'b10), .out(multiplexer_3_out));
  Multiplexer #(.Bits(2)) multiplexer_4 (.sel(reset), .in_0(multiplexer_3_out), .in_1(2'b00), .out(ifin));
  Seven_Seg_Hex seven_seg_hex_1 (.d(out_3), .dp(1'b0));

  // Other names for the same wires on the sheet: i[3:0] = out_3
endmodule
