// Digital circuit 01.dig as structural Verilog
module _01 (
  input  A,
  input  B,
  input  C,
  input  D,
  input  E,
  input  F
);

  wire add_1_c_o, and_1_out, and_2_out, and_3_out, and_4_out, and_5_out, and_6_out, and_7_out, and_8_out,
       not_1_out, not_2_out, not_3_out, not_4_out, or_1_out, or_2_out, or_3_out, or_4_out, or_5_out, or_6_out;
  wire [2:0] add_1_s;

  Add #(.Bits(3)) add_1 (.a({C, B, A}), .b({F, E, D}), .c_i(1'b0), .s(add_1_s), .c_o(add_1_c_o));
  not not_1 (not_1_out, add_1_c_o);
  not not_2 (not_2_out, add_1_s[2]);
  not not_3 (not_3_out, add_1_s[1]);
  not not_4 (not_4_out, add_1_s[0]);
  and and_1 (and_1_out, not_1_out, not_3_out);
  and and_2 (and_2_out, not_1_out, not_2_out);
  or or_1 (or_1_out, not_1_out, not_2_out, not_3_out, not_4_out);
  or or_2 (or_2_out, not_1_out, not_2_out, not_3_out, not_4_out);
  and and_3 (and_3_out, not_1_out, not_3_out);
  and and_4 (and_4_out, not_1_out, not_2_out);
  and and_5 (and_5_out, not_1_out, not_3_out);
  and and_6 (and_6_out, not_1_out, not_2_out);
  and and_7 (and_7_out, not_1_out, not_3_out);
  and and_8 (and_8_out, not_1_out, not_2_out);
  or or_3 (or_3_out, and_1_out, and_2_out);
  or or_4 (or_4_out, and_3_out, and_4_out);
  or or_5 (or_5_out, and_5_out, and_6_out);
  or or_6 (or_6_out, and_7_out, and_8_out);
  Seven_Seg seven_seg_1 (
    .a(or_3_out), .b(or_1_out), .c(or_2_out), .d(or_4_out), .e(or_5_out), .f(or_6_out), .g(1'b0), .dp(1'b0));
endmodule
