// Digital circuit 02.dig as structural Verilog
module _02 (
  input  A,
  input  B,
  input  C
);

  wire demultiplexer_1_out_2, demultiplexer_1_out_4, demultiplexer_1_out_5, demultiplexer_1_out_6,
       demultiplexer_2_out_0, demultiplexer_2_out_2, demultiplexer_2_out_4, demultiplexer_2_out_6,
       demultiplexer_2_out_7, or_1_out, or_2_out;

  Demultiplexer #(.Selector_Bits(3)) demultiplexer_1 (
    .sel({C, B, A}), .in(1'b1), .out_2(demultiplexer_1_out_2), .out_4(demultiplexer_1_out_4),
    .out_5(demultiplexer_1_out_5), .out_6(demultiplexer_1_out_6));  // open: out_0, out_1, out_3, out_7
  Demultiplexer #(.Selector_Bits(3)) demultiplexer_2 (
    .sel({C, B, A}), .in(1'b1), .out_0(demultiplexer_2_out_0), .out_2(demultiplexer_2_out_2),
    .out_4(demultiplexer_2_out_4), .out_6(demultiplexer_2_out_6), .out_7(demultiplexer_2_out_7));  // open: out_1, out_3, out_5
  or or_1 (or_1_out, demultiplexer_1_out_2, demultiplexer_1_out_4, demultiplexer_1_out_5, demultiplexer_1_out_6);
  or or_2 (or_2_out, demultiplexer_2_out_0, demultiplexer_2_out_2, demultiplexer_2_out_4, demultiplexer_2_out_6, demultiplexer_2_out_7);
  // Probe on or_1_out
  // Probe on or_2_out

  // Other names for the same wires on the sheet: sel[2:0] = {C, B, A}
endmodule
